# Fritzing sketch team6Circuit (saved by Fritzing 0.9.3b)
breadboards: 1

parts:
  U1 = ESP8266 NodeMCU LoLin module
  S1 = H-Bridge with L298N
  S2 = H-Bridge with L298N
  VCC2 = 4 x AAA Battery Mount
  M6 = DC Motor
  M8 = DC Motor
  Part1 = MQ-4
  M9 = DC Motor
  M12 = DC Motor
  ESP32_-_Back1 = ESP32 - CAM

nets:
  N1: U1.D0, S2.ENA
  N2: U1.D1, S2.IN1
  N3: U1.D2, S2.IN2
  N4: U1.D3, S2.IN3
  N5: U1.D4, S2.IN4
  N6: U1.D5, S2.ENB
  N7: U1.TX, Part1.DO
  GND: U1.GND, Part1.GND, ESP32_-_Back1.GPIO12, ESP32_-_Back1.GND
  5V: U1.Vin, S2.5V, Part1.VCC, ESP32_-_Back1.5V
  N8: S1.M1-01, M12.pin_2
  N9: S1.M1-02, M12.pin_1
  N10: S1.M2-01, M9.pin_2
  N11: S1.M2-02, M9.pin_1
  N12: S2.12V, VCC2.+
  N13: S2.GND, VCC2.-
  N14: S2.M1-01, M6.pin_2
  N15: S2.M1-02, M6.pin_1
  N16: S2.M2-01, M8.pin_2
  N17: S2.M2-02, M8.pin_1

notes:
  [L298N Motor driver 2]
  [L298N Motor Driver 1]
  [Mq4 gas sensor]
  [Side shaft driving motor]
  [DC motor for cleaning 2 ]
  [DC motor for Extension]
  [ESP32 cam setup]
  [power supply (12v)]

custom parts:
  ESP8266 NodeMCU LoLin module: ESP8266 based NodeMCU
  H-Bridge with L298N: h-bridge
  ESP32 - CAM: The ESP32-CAM has a very competitive small-size camera module that can operate independently as a minimum system with a footprint of only 27*40.5*4.5mm and a deep sleep current of up to 6mA.
